// Logisim project Template.circ as structural Verilog: 4 circuits, main circuit main
module main (
  input  in_1,
  output [14:0] out_2,
  output [15:0] out_3
);

  wire clk;

  // Text text_1: pin names not known
  // Text text_2: pin names not known
  // Text text_3: pin names not known
  // Text text_4: pin names not known
  // Text text_5: pin names not known
  Clock #(.highDuration(4), .lowDuration(4)) u_clk (.out(clk));
  Clock sysclk ();  // open: out
  FETCH_16BITS fetch_16bits_1 (.clk(clk), .CLR(in_1), .PC_IN(out_2), .FETCH_OUT(out_3));

  // Notes on the sheet:
  //   LABO ARO 2 - FETCH
  //   HEIG-VD / Institut REDS
  //   Date : 25.02.2014
  //   Ne pas modifier les noms des clocks
endmodule

module FETCH_16BITS (
  input  clk,
  input  CLR,
  output [14:0] PC_IN,
  output [15:0] FETCH_OUT
);

  wire [0:0] PC_q;
  wire [15:0] adder_1_out;

  // Text text_1: pin names not known
  // Text text_2: pin names not known
  // Text text_3: pin names not known
  // Text text_4: pin names not known
  // Text text_5: pin names not known
  Adder #(.width(16)) adder_1 (.a({PC_IN, PC_q[0]}), .b(16'h2), .out(adder_1_out));  // open: cin, cout
  Register #(.width(16)) PC (.D(adder_1_out), .en(1'b1), .clk(clk), .Q({PC_IN, PC_q[0]}), .clr(CLR));
  BitSelector #(.width(16), .group(15)) bitselector_1 (.sel(1'b0));  // open: in, out
  ROM #(.addrWidth(15), .dataWidth(16)) MEM_INSTRU (.addr(PC_IN), .data(FETCH_OUT));

  // Notes on the sheet:
  //   contents of MEM_INSTRU (hex, n*v repeats v):
  //   2103 188b 18cc 2502
endmodule

module FETCH_JUMP_16BITS (
  input  clk,
  input  JUMP,
  input  CLR,
  output [14:0] PC_IN,
  output [15:0] FETCH_OUT
);

  wire binst_1_op;
  wire [0:0] PC_q;
  wire [15:0] adder_1_out, bit_extender_1_out, multiplexer_1_out, multiplexer_2_out, multiplier_1_out,
       multiplier_2_out;

  // Text text_1: pin names not known
  // Text text_2: pin names not known
  // Text text_3: pin names not known
  // Text text_4: pin names not known
  // Text text_5: pin names not known
  Adder #(.width(16)) adder_1 (.a({PC_IN, PC_q[0]}), .b(16'h2), .out(adder_1_out));  // open: cin, cout
  Multiplier #(.width(16)) multiplier_1 (.a(16'h2), .b(16'h30), .out(multiplier_1_out));  // open: cin, cout
  Multiplexer #(.width(16), .enable("false")) multiplexer_1 (
    .in0(adder_1_out), .in1(multiplier_1_out), .out(multiplexer_1_out), .sel(JUMP));
  Multiplier #(.width(16)) multiplier_2 (.a(16'h2), .b(bit_extender_1_out), .out(multiplier_2_out));  // open: cin, cout
  Register #(.width(16)) PC (.D(multiplexer_2_out), .en(1'b1), .clk(clk), .Q({PC_IN, PC_q[0]}), .clr(CLR));
  Multiplexer #(.width(16), .enable("false")) multiplexer_2 (
    .in0(multiplexer_1_out), .in1(multiplier_2_out), .out(multiplexer_2_out), .sel(binst_1_op));
  ROM #(.addrWidth(15), .dataWidth(16)) MEM_INSTRU (.addr(PC_IN), .data(FETCH_OUT));
  BINST binst_1 (.INST(FETCH_OUT), .OP(binst_1_op));
  // Probe on FETCH_OUT[10:0]
  assign bit_extender_1_out = {{5{FETCH_OUT[10]}}, FETCH_OUT[10:0]};  // Bit_Extender bit_extender_1

  // Notes on the sheet:
  //   contents of MEM_INSTRU (hex, n*v repeats v):
  //   3 ff8b ffcc 2
endmodule

module BINST (
  input  [15:0] INST,
  output OP
);

  wire not_1_out, not_2_out;

  // Text text_1: pin names not known
  // Text text_2: pin names not known
  // Text text_3: pin names not known
  // Text text_4: pin names not known
  // Text text_5: pin names not known
  not not_1 (not_1_out, INST[11]);
  not not_2 (not_2_out, INST[12]);
  and and_1 (OP, not_1_out, not_2_out, INST[13], INST[14], INST[15]);
endmodule
